# Fritzing sketch greeny_wiring (saved by Fritzing 1.0.0rc)
breadboards: 1

parts:
  Capacitive_Soil_Moisture_Sensor1 = DFRobot Capacitive Soil Moisture Sensor V1.0 [part_number=SEN0193]
  S1 = Pushbutton [package="[THT]"]
  Mod1 = Raspberry Pi Pico W
  DHT11_1 = DHT11 module
  Part1 = KY-018 Photoresistor Module [package="Breakout board"]
  R1 = Resistor [tolerance=±5% power=0.25W resistance=0.01M package=THT]

nets:
  N1: Capacitive_Soil_Moisture_Sensor1.A, Mod1.pin_35
  VCC: Capacitive_Soil_Moisture_Sensor1.VCC, S1.Pin_1, S1.Pin_2, Mod1.pin_36, DHT11_1.DATA, Part1.Vin, R1.Pin_0
  GND: Capacitive_Soil_Moisture_Sensor1.GND, Mod1.pin_3, Mod1.pin_8, Mod1.pin_13, Mod1.pin_18, Mod1.pin_23, Mod1.pin_28, Mod1.pin_33, Mod1.pin_38, DHT11_1.GND, Part1.-
  N2: S1.Pin_3, S1.Pin_4, Mod1.pin_29, R1.Pin_1
  N3: Mod1.pin_31, Part1.S
  N4: Mod1.pin_32, DHT11_1.VCC

custom parts:
  DFRobot Capacitive Soil Moisture Sensor V1.0: DFRobot Capacitive Soil Moisture Sensor V1.0 This product measures soil moisture levels by capacitive sensing, rather than resistive sensing like other types of moisture sensor. It is made of a corrosion resistant material giving it a long service life. Insert it into soil and impress your friends with the real-time soil moisture data! The product includes an on-board voltage regulator which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
  Raspberry Pi Pico W: Raspberry Pi Pico W. Based around the RP2040 microcontroller the Pico W is a low cost microcontroller device bringing Raspberry Pi quality, cost, and easy of use to the microcontroller space. The areas marked KEEPOUT in pcb silkscreen should not have traces running through them to avoid shorts on a soldered in module!
  DHT11 module: https://cdn-learn.adafruit.com/downloads/pdf/dht.pdf DHT11 black pcb module reference by:https://github.com/adafruit/Fritzing-Library/blob/master/parts/DHT11%20Humitidy%20and%20Temperature%20Sensor.fzpz
  KY-018 Photoresistor Module: KY-018 Photoresistor module, used to measure light intensity. It can determine the presence or absence of light.
